# Fritzing sketch Wiring_ESP32 (saved by Fritzing 0.9.10b)

parts:
  U1 = ESP32-38PinWide [part_number=ESP32-38PinWide]
  Bauteil1 = NRF24L01+ Breakout Board
  Grove1 = TM1637 7segment 4digit display
  LED1 = smd LED [color="Red (633nm)" package="1206 [SMD]"]
  LED2 = smd LED [color="Green (560nm)" package="1206 [SMD]"]
  R1 = Resistor [tolerance=±5% resistance=220 package="0402 [SMD]"]
  R2 = Resistor [tolerance=±5% resistance=220 package="0402 [SMD]"]

nets:
  VCC: U1.3.3, Bauteil1.VCC, Grove1.Vcc
  N1: U1.GPIO32, Grove1.DIO
  N2: U1.GPIO33, Grove1.CLK
  N3: U1.GPIO25, R1.Pin_1
  N4: U1.GPIO26, R2.Pin_1
  GND: U1.GND, Bauteil1.GND, Grove1.GND, LED1.cathode, LED2.cathode
  N5: U1.GPIO4, Bauteil1.CE
  N6: U1.GPIO16, Bauteil1.IRQ
  N7: U1.GPIO5, Bauteil1.CS
  N8: U1.GPIO18, Bauteil1.SCK
  N9: U1.GPIO19, Bauteil1.MISO
  N10: U1.GPIO23, Bauteil1.MOSI
  N11: LED1.anode, R1.Pin_0
  N12: LED2.anode, R2.Pin_0

custom parts:
  ESP32-38PinWide: Generic 38-Pin ESP32 with wide format (only access to one side of pins on a breadboard) based on Stephen Lilley's HiLetgo ESP-WROOM-32 ESP32 ESP-32S Development Board.
